// Logisim project +1 bit.circ as structural Verilog: 1 circuit, main circuit main
module main (
  input  [19:0] PC,
  output [19:0] PC_1
);

  Adder #(.width(20)) adder_1 (.a(20'h1), .b(PC), .out(PC_1), .cin(1'b0));  // open: cout

  // Notes on the sheet:
  //   Adding 1 Bit
endmodule
