// Logisim project ALU_V3.circ as structural Verilog: 1 circuit, main circuit main
module main (
  input  [31:0] in_1,
  input  [9:0] ALU_OP,
  input  [31:0] in_3,
  output [31:0] out_4
);

  wire Bigger, comparator_1_eq, comparator_2_lt, Equal, Less, not_1_out, or_2_out;
  wire [31:0] ADD_I, AND_I, bit_extender_3_out, bit_extender_4_out, bit_extender_5_out, bit_extender_6_out,
       Branch_Result, CADD_I, CAND_I, OR_I, R_Arith, R_Logical, SEQ_I, Shift_Result, shifter_1_out,
       shifter_2_out, shifter_3_out, shifter_4_out, SLT_I, XOR_I;

  assign AND_I = in_1 & in_3;  // AND_Gate AND, 32 bits wide
  assign CAND_I = ~in_1 & in_3;  // AND_Gate CAND, 32 bits wide
  assign OR_I = in_1 | in_3;  // OR_Gate OR, 32 bits wide
  assign XOR_I = in_1 ^ in_3;  // XOR_Gate XOR, 32 bits wide
  Comparator #(.width(32)) comparator_1 (.a(in_1), .b(in_3), .eq(comparator_1_eq));  // open: gt, lt
  Comparator #(.width(32)) comparator_2 (.a(in_1), .b(in_3), .lt(comparator_2_lt));  // open: gt, eq
  Comparator #(.width(32)) comparator_3 (.a(in_1), .b(in_3), .gt(Bigger), .eq(Equal), .lt(Less));
  Adder #(.width(32)) adder_1 (.a(in_1), .b(in_3), .out(ADD_I));  // open: cin, cout
  Subtractor #(.width(32)) subtractor_1 (.a(in_3), .b(in_1), .out(CADD_I));  // open: bin, bout
  assign SEQ_I = {{31{1'b0}}, comparator_1_eq};  // Bit_Extender bit_extender_1
  assign SLT_I = {{31{1'b0}}, comparator_2_lt};  // Bit_Extender bit_extender_2
  Shifter #(.width(32)) shifter_1 (.in(in_1), .\dist (in_3[4:0]), .out(shifter_1_out));
  Shifter #(.width(32), .shift("lr")) shifter_2 (.in(in_1), .\dist (in_3[4:0]), .out(shifter_2_out));
  Shifter #(.width(32), .shift("ar")) shifter_3 (.in(in_1), .\dist (in_3[4:0]), .out(shifter_3_out));
  Shifter #(.width(32), .shift("rr")) shifter_4 (.in(in_1), .\dist (in_3[4:0]), .out(shifter_4_out));
  not not_1 (not_1_out, Equal);
  or or_2 (or_2_out, Equal, Bigger);
  assign bit_extender_3_out = {{31{1'b0}}, Equal};  // Bit_Extender bit_extender_3
  assign bit_extender_4_out = {{31{1'b0}}, not_1_out};  // Bit_Extender bit_extender_4
  assign bit_extender_5_out = {{31{1'b0}}, or_2_out};  // Bit_Extender bit_extender_5
  assign bit_extender_6_out = {{31{1'b0}}, Less};  // Bit_Extender bit_extender_6
  Multiplexer #(.select(2), .width(32), .enable("false")) multiplexer_1 (
    .in0(AND_I), .in1(CAND_I), .in2(OR_I), .in3(XOR_I), .out(R_Logical), .sel(ALU_OP[3:2]));
  Multiplexer #(.select(2), .width(32), .enable("false")) multiplexer_2 (
    .in0(ADD_I), .in1(CADD_I), .in2(SEQ_I), .in3(SLT_I), .out(R_Arith), .sel(ALU_OP[5:4]));
  Multiplexer #(.select(2), .width(32), .enable("false")) multiplexer_3 (
    .in0(shifter_1_out), .in1(shifter_2_out), .in2(shifter_3_out), .in3(shifter_4_out), .out(Shift_Result),
    .sel(ALU_OP[7:6]));
  Multiplexer #(.select(2), .width(32), .enable("false")) multiplexer_4 (
    .in0(bit_extender_3_out), .in1(bit_extender_4_out), .in2(bit_extender_5_out), .in3(bit_extender_6_out),
    .out(Branch_Result), .sel(ALU_OP[9:8]));
  Multiplexer #(.select(2), .width(32), .enable("false")) multiplexer_5 (
    .in0(R_Logical), .in1(R_Arith), .in2(Shift_Result), .in3(Branch_Result), .out(out_4), .sel(ALU_OP[1:0]));

  // Other names for the same wires on the sheet: A[31:0] = in_1; ALU_Select[1:0] = ALU_OP[1:0];
  //   Logic_Select[1:0] = ALU_OP[3:2]; Arith_Select[1:0] = ALU_OP[5:4]; Shift_Select[1:0] = ALU_OP[7:6];
  //   Branch_Select[1:0] = ALU_OP[9:8]; B[31:0] = in_3; B_5_LSB[4:0] = in_3[4:0]
endmodule
