// Logisim project ALU.circ as structural Verilog: 2 circuits, main circuit ALU
module ALU (
  input  [31:0] in_1,
  input  [9:0] ALU_OP,
  input  [31:0] in_3,
  output [31:0] out_4
);

  wire Bigger, comparator_1_eq, comparator_2_lt, Equal, Less, not_1_out, or_2_out;
  wire [31:0] adder_1_out, AND_out, bit_extender_1_out, bit_extender_2_out, bit_extender_3_out,
       bit_extender_4_out, bit_extender_5_out, bit_extender_6_out, Branch_Result, CAND_out, OR_out, R_Arith,
       R_Logical, Shift_Result, shifter_1_out, shifter_2_out, shifter_3_out, shifter_4_out, subtractor_1_out,
       XOR_out;

  assign AND_out = in_1 & in_3;  // AND_Gate AND, 32 bits wide
  assign CAND_out = ~in_1 & in_3;  // AND_Gate CAND, 32 bits wide
  assign OR_out = in_1 | in_3;  // OR_Gate OR, 32 bits wide
  assign XOR_out = in_1 ^ in_3;  // XOR_Gate XOR, 32 bits wide
  Comparator #(.width(32)) comparator_1 (.a(in_1), .b(in_3), .eq(comparator_1_eq));  // open: gt, lt
  Comparator #(.width(32)) comparator_2 (.a(in_1), .b(in_3), .lt(comparator_2_lt));  // open: gt, eq
  Comparator #(.width(32)) comparator_3 (.a(in_1), .b(in_3), .gt(Bigger), .eq(Equal), .lt(Less));
  Adder #(.width(32)) adder_1 (.a(in_1), .b(in_3), .out(adder_1_out));  // open: cin, cout
  Subtractor #(.width(32)) subtractor_1 (.a(in_3), .b(in_1), .out(subtractor_1_out));  // open: bin, bout
  assign bit_extender_1_out = {{31{1'b0}}, comparator_1_eq};  // Bit_Extender bit_extender_1
  assign bit_extender_2_out = {{31{1'b0}}, comparator_2_lt};  // Bit_Extender bit_extender_2
  Shifter #(.width(32)) shifter_1 (.in(in_1), .\dist (in_3[4:0]), .out(shifter_1_out));
  Shifter #(.width(32), .shift("lr")) shifter_2 (.in(in_1), .\dist (in_3[4:0]), .out(shifter_2_out));
  Shifter #(.width(32), .shift("ar")) shifter_3 (.in(in_1), .\dist (in_3[4:0]), .out(shifter_3_out));
  Shifter #(.width(32), .shift("rr")) shifter_4 (.in(in_1), .\dist (in_3[4:0]), .out(shifter_4_out));
  not not_1 (not_1_out, Equal);
  or or_2 (or_2_out, Equal, Bigger);
  assign bit_extender_3_out = {{31{1'b0}}, Equal};  // Bit_Extender bit_extender_3
  assign bit_extender_4_out = {{31{1'b0}}, not_1_out};  // Bit_Extender bit_extender_4
  assign bit_extender_5_out = {{31{1'b0}}, or_2_out};  // Bit_Extender bit_extender_5
  assign bit_extender_6_out = {{31{1'b0}}, Less};  // Bit_Extender bit_extender_6
  Multiplexer #(.select(2), .width(32), .enable("false")) multiplexer_1 (
    .in0(AND_out), .in1(CAND_out), .in2(OR_out), .in3(XOR_out), .out(R_Logical), .sel(ALU_OP[3:2]));
  Multiplexer #(.select(2), .width(32), .enable("false")) multiplexer_2 (
    .in0(adder_1_out), .in1(subtractor_1_out), .in2(bit_extender_1_out), .in3(bit_extender_2_out),
    .out(R_Arith), .sel(ALU_OP[5:4]));
  Multiplexer #(.select(2), .width(32), .enable("false")) multiplexer_3 (
    .in0(shifter_1_out), .in1(shifter_2_out), .in2(shifter_3_out), .in3(shifter_4_out), .out(Shift_Result),
    .sel(ALU_OP[7:6]));
  Multiplexer #(.select(2), .width(32), .enable("false")) multiplexer_4 (
    .in0(bit_extender_3_out), .in1(bit_extender_4_out), .in2(bit_extender_6_out), .in3(bit_extender_5_out),
    .out(Branch_Result), .sel(ALU_OP[9:8]));
  Multiplexer #(.select(2), .width(32), .enable("false")) multiplexer_5 (
    .in0(R_Logical), .in1(R_Arith), .in2(Shift_Result), .in3(Branch_Result), .out(out_4), .sel(ALU_OP[1:0]));

  // Other names for the same wires on the sheet: A[31:0] = in_1; ALU_Select[1:0] = ALU_OP[1:0];
  //   Logic_Select[1:0] = ALU_OP[3:2]; Arith_Select[1:0] = ALU_OP[5:4]; Shift_Select[1:0] = ALU_OP[7:6];
  //   Branch_Select[1:0] = ALU_OP[9:8]; B[31:0] = in_3; B_5_LSB[4:0] = in_3[4:0]
endmodule

module ALU_Control (
  input  [4:0] Op_Code,
  input  [1:0] Func_Code,
  output [9:0] ALU_Op
);

  wire and_1_out, and_2_out, and_3_out, and_4_out, and_5_out, and_6_out, and_7_out, and_8_out, and_9_out,
       not_1_out, not_2_out, not_3_out, not_4_out, not_5_out, not_6_out, or_1_out, or_2_out, or_3_out,
       or_4_out, or_7_out;

  not not_1 (not_1_out, Op_Code[3]);
  not not_2 (not_2_out, Op_Code[3]);
  not not_3 (not_3_out, Op_Code[2]);
  not not_4 (not_4_out, Op_Code[2]);
  and and_1 (and_1_out, Op_Code[3], Op_Code[2]);
  not not_5 (not_5_out, Op_Code[2]);
  not not_6 (not_6_out, Op_Code[2]);
  or or_1 (or_1_out, Op_Code[0], ~Op_Code[0]);  // OR_Gate
  and and_2 (and_2_out, not_1_out, Func_Code[1]);
  and and_3 (and_3_out, not_2_out, Func_Code[0]);
  and and_4 (and_4_out, Op_Code[3], Op_Code[0]);
  and and_5 (and_5_out, not_3_out, Func_Code[1]);
  and and_6 (and_6_out, not_4_out, Func_Code[0]);
  or or_2 (or_2_out, and_1_out, Op_Code[4]);
  and and_7 (and_7_out, not_5_out, Op_Code[0]);
  and and_8 (and_8_out, Op_Code[3], not_6_out);
  and and_9 (and_9_out, or_1_out, ~Op_Code[1], Op_Code[2], ~Op_Code[3], Op_Code[4]);  // AND_Gate
  or or_3 (or_3_out, and_2_out, Op_Code[1]);
  or or_4 (or_4_out, and_3_out, and_4_out);
  or or_5 (ALU_Op[3], and_5_out, Op_Code[1]);
  or or_6 (ALU_Op[2], and_6_out, Op_Code[0]);
  or or_7 (or_7_out, and_7_out, and_8_out, Op_Code[4]);
  Multiplexer #(.enable("false")) multiplexer_1 (.in0(or_7_out), .in1(1'b1), .out(ALU_Op[0]), .sel(and_9_out));
  Multiplexer #(.enable("false")) multiplexer_2 (.in0(or_2_out), .in1(1'b0), .out(ALU_Op[1]), .sel(and_9_out));
  Multiplexer #(.enable("false")) multiplexer_3 (.in0(or_3_out), .in1(1'b0), .out(ALU_Op[5]), .sel(and_9_out));
  Multiplexer #(.enable("false")) multiplexer_4 (.in0(or_4_out), .in1(1'b0), .out(ALU_Op[4]), .sel(and_9_out));

  assign ALU_Op[9:6] = {Op_Code[1:0], Op_Code[1:0]};

  // Notes on the sheet:
  //   Branch_Select1
  //   Branch_Select0
  //   Shift_Select1
  //   Shift_Select0
  //   Arith_Select1
  //   Arith_Select0
  //   Logic_Select1
  //   Logic_Select0
  //   ALU_Select1
  //   ALU_Select0
endmodule
