// Logisim project ALU_V3.circ as structural Verilog: 1 circuit, main circuit main
module main (
  input  [31:0] in_1,
  input  [4:0] in_2,
  input  [31:0] in_3,
  input  [1:0] in_4,
  output [31:0] out_5
);

  wire Bigger, comparator_1_eq, comparator_2_lt, Equal, Less, not_1_out, or_2_out;
  wire [31:0] ADD_I, AND_I, BEQ, BGE, BLT, BNE, CADD_I, CAND_I, OR_I, R_Arith, R_Logical, ROR, SEQ_I, SLL,
       SLT_I, SRA, SRL, XOR_I;

  assign AND_I = in_1 & in_3;  // AND_Gate AND, 32 bits wide
  assign CAND_I = ~in_1 & in_3;  // AND_Gate CAND, 32 bits wide
  assign OR_I = in_1 | in_3;  // OR_Gate OR, 32 bits wide
  assign XOR_I = in_1 ^ in_3;  // XOR_Gate XOR, 32 bits wide
  Comparator #(.width(32)) comparator_1 (.a(in_1), .b(in_3), .eq(comparator_1_eq));  // open: gt, lt
  Comparator #(.width(32)) comparator_2 (.a(in_1), .b(in_3), .lt(comparator_2_lt));  // open: gt, eq
  Comparator #(.width(32)) comparator_3 (.a(in_1), .b(in_3), .gt(Bigger), .eq(Equal), .lt(Less));
  Adder #(.width(32)) adder_1 (.a(in_1), .b(in_3), .out(ADD_I));  // open: cin, cout
  Subtractor #(.width(32)) subtractor_1 (.a(in_3), .b(in_1), .out(CADD_I));  // open: bin, bout
  assign SEQ_I = {{31{1'b0}}, comparator_1_eq};  // Bit_Extender bit_extender_1
  assign SLT_I = {{31{1'b0}}, comparator_2_lt};  // Bit_Extender bit_extender_2
  Shifter #(.width(32)) shifter_1 (.in(in_1), .\dist (in_3[4:0]), .out(SLL));
  Shifter #(.width(32), .shift("lr")) shifter_2 (.in(in_1), .\dist (in_3[4:0]), .out(SRL));
  Shifter #(.width(32), .shift("ar")) shifter_3 (.in(in_1), .\dist (in_3[4:0]), .out(SRA));
  Shifter #(.width(32), .shift("rr")) shifter_4 (.in(in_1), .\dist (in_3[4:0]), .out(ROR));
  not not_1 (not_1_out, Equal);
  or or_2 (or_2_out, Equal, Bigger);
  assign BEQ = {{31{1'b0}}, Equal};  // Bit_Extender bit_extender_3
  assign BNE = {{31{1'b0}}, not_1_out};  // Bit_Extender bit_extender_4
  assign BGE = {{31{1'b0}}, or_2_out};  // Bit_Extender bit_extender_5
  assign BLT = {{31{1'b0}}, Less};  // Bit_Extender bit_extender_6
  Multiplexer #(.select(2), .width(32), .enable("false")) multiplexer_1 (
    .in0(AND_I), .in1(CAND_I), .in2(OR_I), .in3(XOR_I), .out(R_Logical), .sel(in_4));
  Multiplexer #(.select(2), .width(32), .enable("false")) multiplexer_2 (
    .in0(ADD_I), .in1(CADD_I), .in2(SEQ_I), .in3(SLT_I), .out(R_Arith), .sel(in_4));
  Multiplexer #(.select(5), .width(32), .enable("false")) multiplexer_3 (
    .in0(R_Logical), .in1(R_Arith), .in2({32{1'b0}}), .in3({32{1'b0}}), .in4(AND_I), .in5(CAND_I),
    .in6(OR_I), .in7(XOR_I), .in8(ADD_I), .in9(CADD_I), .in10(SEQ_I), .in11(SLT_I), .in12(SLL), .in13(SRL),
    .in14(SRA), .in15(ROR), .in16(BEQ), .in17(BNE), .in18(BLT), .in19(BGE), .in20({32{1'b0}}),
    .in21({32{1'b0}}), .in22({32{1'b0}}), .in23({32{1'b0}}), .in24({32{1'b0}}), .in25({32{1'b0}}),
    .in26({32{1'b0}}), .in27({32{1'b0}}), .in28({32{1'b0}}), .in29({32{1'b0}}), .in30({32{1'b0}}),
    .in31({32{1'b0}}), .out(out_5), .sel(in_2));

  // Other names for the same wires on the sheet: A[31:0] = in_1; B[31:0] = in_3; B_5_LSB[4:0] = in_3[4:0];
  //   Func_Code[1:0] = in_4; OP_Code[4:0] = in_2
endmodule
