// Logisim project Instruction_Decoder.circ as structural Verilog: 1 circuit, main circuit Instruction_Decoder
module Instruction_Decoder (
  input  [15:0] in_1,
  output [4:0] OP_code,
  output [2:0] a3,
  output [2:0] b3,
  output [4:0] imm,
  output [1:0] f,
  output [2:0] d3,
  output [10:0] out_8
);


  assign a3 = in_1[10:8];
  assign b3 = in_1[7:5];
  assign d3 = in_1[4:2];
  assign f = in_1[1:0];
  assign imm = in_1[4:0];
  assign OP_code = in_1[15:11];
  assign out_8 = in_1[10:0];
endmodule
