// Logisim project Main_Control.circ as structural Verilog: 1 circuit, main circuit Main_Control
module Main_Control (
  input  [4:0] Op_Code,
  output MEM_LD,
  output MEM_Write,
  output ALU_Src,
  output RegDst,
  output RegWrite,
  output WB_Data,
  output Jump,
  output Zero_Sign_Ext,
  output Register,
  output Branch,
  output PC_Or_Result,
  output Rb_Or_R7
);

  wire and_1_out, and_6_out, and_7_out, not_1_out, not_2_out, not_3_out, not_4_out, not_5_out, not_6_out,
       not_7_out, not_8_out, not_9_out, not_10_out, not_11_out, not_12_out, not_13_out, not_14_out,
       not_15_out, not_16_out, or_3_out;

  not not_1 (not_1_out, Op_Code[2]);
  or or_1 (Zero_Sign_Ext, Op_Code[4], not_1_out);
  and and_1 (and_1_out, Op_Code[0], ~Op_Code[1], Op_Code[2], Op_Code[3], Op_Code[4]);  // AND_Gate
  not not_2 (not_2_out, Op_Code[3]);
  not not_3 (not_3_out, Op_Code[0]);
  not not_4 (not_4_out, Op_Code[3]);
  or or_2 (ALU_Src, Op_Code[2], Op_Code[3]);
  not not_5 (not_5_out, Op_Code[3]);
  not not_6 (not_6_out, Op_Code[2]);
  not not_7 (not_7_out, Op_Code[3]);
  not not_8 (not_8_out, Op_Code[0]);
  not not_9 (not_9_out, Op_Code[2]);
  not not_10 (not_10_out, Op_Code[3]);
  not not_11 (not_11_out, Op_Code[1]);
  not not_12 (not_12_out, Op_Code[2]);
  not not_13 (not_13_out, Op_Code[3]);
  not not_14 (not_14_out, Op_Code[2]);
  and and_2 (PC_Or_Result, Op_Code[4], Op_Code[3], Op_Code[0]);
  not not_15 (not_15_out, Op_Code[1]);
  and and_3 (MEM_LD, Op_Code[4], not_2_out, Op_Code[2], not_3_out);
  and and_4 (MEM_Write, Op_Code[4], not_4_out, Op_Code[2], Op_Code[0]);
  and and_5 (RegDst, not_5_out, not_6_out);
  not not_16 (not_16_out, Op_Code[4]);
  and and_6 (and_6_out, not_7_out, Op_Code[2], not_8_out);
  and and_7 (and_7_out, Op_Code[3], not_9_out);
  and and_8 (WB_Data, Op_Code[4], not_10_out);
  and and_9 (Jump, Op_Code[4], Op_Code[3], not_11_out);
  and and_10 (Register, Op_Code[4], Op_Code[3], not_12_out);
  and and_11 (Branch, Op_Code[4], not_13_out, not_14_out);
  and and_12 (Rb_Or_R7, Op_Code[4], Op_Code[3], not_15_out, Op_Code[0]);
  or or_3 (or_3_out, not_16_out, and_6_out, and_7_out);
  Multiplexer #(.enable("false")) multiplexer_1 (.in0(or_3_out), .in1(1'b1), .out(RegWrite), .sel(and_1_out));
endmodule
