// Logisim project PC_Register.circ as structural Verilog: 3 circuits, main circuit PC_Register
module PC_Register (
  input  [4:0] in_1,
  input  [10:0] in_2,
  input  [31:0] in_3,
  input  Branch,
  input  Jump,
  input  Register,
  input  in_7,
  output [19:0] PC_2,
  output [19:0] out_9
);

  wire [1:0] PC_SRC;
  wire [4:0] shifter_2_out;
  wire [10:0] shifter_1_out;
  wire [18:0] multiplexer_1_out, PC___Imm5, PC___Imm11, Sign_Ext_Imm5__1, Sign_Ext_Imm11__1;

  Multiplexer #(.select(2), .width(19), .enable("false")) multiplexer_1 (
    .in0(PC_2[19:1]), .in1(PC___Imm5), .in2(PC___Imm11), .in3(in_3[18:0]), .out(multiplexer_1_out),
    .sel(PC_SRC));
  Shifter #(.width(11)) shifter_1 (.in(in_2), .\dist (4'b0001), .out(shifter_1_out));
  assign Sign_Ext_Imm11__1 = {{8{shifter_1_out[10]}}, shifter_1_out};  // Bit_Extender bit_extender_1
  Register #(.width(20)) register_1 (.D({multiplexer_1_out, 1'b0}), .en(1'b1), .Q(out_9), .clk(in_7), .clr(1'b0));
  Adder #(.width(19)) adder_1 (.a(out_9[19:1]), .b(Sign_Ext_Imm5__1), .out(PC___Imm5));  // open: cin, cout
  Adder #(.width(19)) adder_2 (.a(out_9[19:1]), .b(Sign_Ext_Imm11__1), .out(PC___Imm11));  // open: cin, cout
  Adder #(.width(19)) adder_3 (.a(out_9[19:1]), .b(19'h1), .out(PC_2[19:1]));  // open: cin, cout
  Shifter #(.width(5)) shifter_2 (.in(in_1), .\dist (3'b001), .out(shifter_2_out));
  assign Sign_Ext_Imm5__1 = {{14{shifter_2_out[4]}}, shifter_2_out};  // Bit_Extender bit_extender_2
  PC_SRC_V2 pc_src_v2_1 (.Branch(Branch), .Jump(Jump), .Register(Register), .out_4(PC_SRC));
  // Probe on PC_SRC

  assign PC_2[0] = 1'b0;

  // Other names for the same wires on the sheet: Rb[18:0] = in_3[18:0]; PC[18:0] = out_9[19:1];
  //   PC___2[18:0] = PC_2[19:1]
endmodule

module PC_SRC (
  input  Branch,
  input  Jump,
  output [1:0] out_3
);

  wire not_1_out, not_2_out;

  not not_1 (not_1_out, Branch);
  not not_2 (not_2_out, Jump);
  and and_1 (out_3[1], not_1_out, Jump);
  and and_2 (out_3[0], Branch, not_2_out);
endmodule

module PC_SRC_V2 (
  input  Branch,
  input  Jump,
  input  Register,
  output [1:0] out_4
);

  wire and_1_out, and_2_out, and_3_out, and_4_out, not_1_out, not_2_out, not_3_out, not_4_out, not_5_out,
       not_6_out, not_7_out, not_8_out;

  not not_1 (not_1_out, Branch);
  not not_2 (not_2_out, Jump);
  not not_3 (not_3_out, Branch);
  not not_4 (not_4_out, Register);
  not not_5 (not_5_out, Branch);
  not not_6 (not_6_out, Jump);
  not not_7 (not_7_out, Jump);
  not not_8 (not_8_out, Register);
  and and_1 (and_1_out, not_1_out, not_2_out, Register);
  and and_2 (and_2_out, not_3_out, Jump, not_4_out);
  and and_3 (and_3_out, not_5_out, not_6_out, Register);
  and and_4 (and_4_out, Branch, not_7_out, not_8_out);
  or or_1 (out_4[1], and_1_out, and_2_out);
  or or_2 (out_4[0], and_3_out, and_4_out);
endmodule
