// Logisim project Register_File.circ as structural Verilog: 1 circuit, main circuit Register_File
module Register_File (
  input  [2:0] Ra,
  input  [2:0] Rb,
  input  [2:0] Rw,
  input  RegWrite,
  input  Clock,
  input  [31:0] in_6,
  output [31:0] BusA,
  output [31:0] BusB
);

  wire and_1_out, and_2_out, and_3_out, and_4_out, and_5_out, and_6_out, and_7_out, decoder_1_out1,
       decoder_1_out2, decoder_1_out3, decoder_1_out4, decoder_1_out5, decoder_1_out6, decoder_1_out7,
       decoder_2_out0, decoder_2_out1, decoder_2_out2, decoder_2_out3, decoder_2_out4, decoder_2_out5,
       decoder_2_out6, decoder_2_out7, decoder_3_out0, decoder_3_out1, decoder_3_out2, decoder_3_out3,
       decoder_3_out4, decoder_3_out5, decoder_3_out6, decoder_3_out7;
  wire [31:0] R1_q, R2_q, R3_q, R4_q, R5_q, R6_q, R7_q;

  Decoder #(.select(3), .enable("false")) decoder_1 (
    .out1(decoder_1_out1), .out2(decoder_1_out2), .out3(decoder_1_out3), .out4(decoder_1_out4),
    .out5(decoder_1_out5), .out6(decoder_1_out6), .out7(decoder_1_out7), .sel(Rw));  // open: out0
  assign BusA = decoder_2_out0 ? {32{1'b0}} : 32'bz;  // Controlled_Buffer controlled_buffer_1
  Decoder #(.select(3), .enable("false")) decoder_2 (
    .out0(decoder_2_out0), .out1(decoder_2_out1), .out2(decoder_2_out2), .out3(decoder_2_out3),
    .out4(decoder_2_out4), .out5(decoder_2_out5), .out6(decoder_2_out6), .out7(decoder_2_out7), .sel(Ra));
  and and_1 (and_1_out, RegWrite, decoder_1_out1);
  and and_2 (and_2_out, decoder_1_out2, RegWrite);
  and and_3 (and_3_out, decoder_1_out3, RegWrite);
  and and_4 (and_4_out, decoder_1_out4, RegWrite);
  and and_5 (and_5_out, decoder_1_out5, RegWrite);
  and and_6 (and_6_out, decoder_1_out6, RegWrite);
  and and_7 (and_7_out, decoder_1_out7, RegWrite);
  Register #(.width(32)) R1 (.D(in_6), .en(and_1_out), .Q(R1_q), .clk(Clock), .clr(1'b0));
  Register #(.width(32)) R2 (.D(in_6), .en(and_2_out), .Q(R2_q), .clk(Clock), .clr(1'b0));
  Register #(.width(32)) R3 (.D(in_6), .en(and_3_out), .Q(R3_q), .clk(Clock), .clr(1'b0));
  Register #(.width(32)) R4 (.D(in_6), .en(and_4_out), .Q(R4_q), .clk(Clock), .clr(1'b0));
  Register #(.width(32)) R5 (.D(in_6), .en(and_5_out), .Q(R5_q), .clk(Clock), .clr(1'b0));
  Register #(.width(32)) R6 (.D(in_6), .en(and_6_out), .Q(R6_q), .clk(Clock), .clr(1'b0));
  Register #(.width(32)) R7 (.D(in_6), .en(and_7_out), .Q(R7_q), .clk(Clock), .clr(1'b0));
  assign BusB = decoder_3_out0 ? {32{1'b0}} : 32'bz;  // Controlled_Buffer controlled_buffer_2
  assign BusA = decoder_2_out1 ? R1_q : 32'bz;  // Controlled_Buffer R1_BusA
  assign BusA = decoder_2_out2 ? R2_q : 32'bz;  // Controlled_Buffer R2_BusA
  assign BusA = decoder_2_out3 ? R3_q : 32'bz;  // Controlled_Buffer R3_BusA
  assign BusA = decoder_2_out4 ? R4_q : 32'bz;  // Controlled_Buffer R4_BusA
  assign BusA = decoder_2_out5 ? R5_q : 32'bz;  // Controlled_Buffer R5_BusA
  assign BusA = decoder_2_out6 ? R6_q : 32'bz;  // Controlled_Buffer R6_BusA
  assign BusA = decoder_2_out7 ? R7_q : 32'bz;  // Controlled_Buffer R7_BusA
  Decoder #(.select(3), .enable("false")) decoder_3 (
    .out0(decoder_3_out0), .out1(decoder_3_out1), .out2(decoder_3_out2), .out3(decoder_3_out3),
    .out4(decoder_3_out4), .out5(decoder_3_out5), .out6(decoder_3_out6), .out7(decoder_3_out7), .sel(Rb));
  assign BusB = decoder_3_out1 ? R1_q : 32'bz;  // Controlled_Buffer R1_BusB
  assign BusB = decoder_3_out2 ? R2_q : 32'bz;  // Controlled_Buffer R2_BusB
  assign BusB = decoder_3_out3 ? R3_q : 32'bz;  // Controlled_Buffer R3_BusB
  assign BusB = decoder_3_out4 ? R4_q : 32'bz;  // Controlled_Buffer R4_BusB
  assign BusB = decoder_3_out5 ? R5_q : 32'bz;  // Controlled_Buffer R5_BusB
  assign BusB = decoder_3_out6 ? R6_q : 32'bz;  // Controlled_Buffer R6_BusB
  assign BusB = decoder_3_out7 ? R7_q : 32'bz;  // Controlled_Buffer R7_BusB

  // Other names for the same wires on the sheet: BusW[31:0] = in_6
endmodule
