// Logisim project Data_Memory.circ as structural Verilog: 1 circuit, main circuit Data_Memory
module Data_Memory (
  input  [19:0] in_1,
  input  in_2,
  input  in_3,
  input  [31:0] in_4,
  input  in_5,
  output [31:0] out_6
);

  RAM #(.addrWidth(20), .dataWidth(32), .bus("separate")) ram_1 (
    .addr(in_1), .din(in_4), .data(out_6), .str(in_2), .clk(in_5), .ld(in_3));  // open: sel, clr
endmodule
