// Logisim project Pipeline.circ as structural Verilog: 1 circuit, main circuit CPU
// lr
module CPU (
);

  wire ALU_Src, Branch, CLK, Jump, main_control_1_zero_sign_ext, MEM_LD, MEM_SW, multiplexer_1_out,
       PC_Or_Result, Rb_Or_R7, RegDst, Register, RegWrite, WB_Data;
  wire [1:0] Fn;
  wire [2:0] instruction_decoder_1_a3, instruction_decoder_1_b3, instruction_decoder_1_d3, multiplexer_5_out,
       multiplexer_6_out, Rd2_q, Rd3_q, Rd4;
  wire [4:0] Imm5, OP;
  wire [9:0] alu_control_1_alu_op;
  wire [10:0] Imm11;
  wire [15:0] Inst_q, rom_1_data;
  wire [19:0] adder_1_out, main_1_pc_1, NPC_q, pc_register_1_out_9, pc_register_1_pc_2, shifter_1_out,
       undriven;
  wire [31:0] alu_1_out_4, ALU_Result, bit_extender_2_out, bit_extender_3_out, Bus_A, Bus_B, D_q, Data,
       ExtImm5, Memory_Out, multiplexer_3_out, multiplexer_4_out, multiplexer_7_out, multiplexer_8_out, PC_2,
       register_file_1_busa, register_file_1_busb;

  Multiplexer #(.enable("false")) multiplexer_1 (
    .in0(1'b0), .in1(ALU_Result[0]), .out(multiplexer_1_out), .sel(Branch));
  Clock clock_1 (.out(CLK));
  _1_bit_main main_1 (.PC(pc_register_1_out_9), .PC_1(main_1_pc_1));
  PC_Register pc_register_1 (
    .in_1(Imm5), .in_2(Imm11), .Branch(multiplexer_1_out), .Jump(Jump), .in_7(CLK),
    .out_9(pc_register_1_out_9), .Register(Register), .in_3(Bus_A), .PC_2(pc_register_1_pc_2));
  Shifter #(.width(20), .shift("lr")) shifter_1 (.in(pc_register_1_out_9), .\dist (5'b00001), .out(shifter_1_out));
  assign PC_2 = {{12{1'b0}}, pc_register_1_pc_2};  // Bit_Extender bit_extender_1
  assign bit_extender_2_out = {{27{1'b0}}, Imm5};  // Bit_Extender bit_extender_2
  assign bit_extender_3_out = {{27{Imm5[4]}}, Imm5};  // Bit_Extender bit_extender_3
  Main_Control main_control_1 (
    .MEM_LD(MEM_LD), .MEM_Write(MEM_SW), .ALU_Src(ALU_Src), .RegDst(RegDst), .RegWrite(RegWrite),
    .WB_Data(WB_Data), .Jump(Jump), .Register(Register), .Branch(Branch), .PC_Or_Result(PC_Or_Result),
    .Rb_Or_R7(Rb_Or_R7), .Op_Code(OP), .Zero_Sign_Ext(main_control_1_zero_sign_ext));
  Multiplexer #(.width(32), .enable("false")) multiplexer_2 (
    .in0(bit_extender_2_out), .in1(bit_extender_3_out), .out(ExtImm5), .sel(main_control_1_zero_sign_ext));
  ROM #(.addrWidth(20), .dataWidth(16)) rom_1 (.addr(shifter_1_out), .data(rom_1_data));  // open: sel
  Register #(.width(20)) NPC (.D(main_1_pc_1), .Q(NPC_q), .clk(CLK));  // open: en, clr
  Register #(.width(16)) Inst (.D(rom_1_data), .Q(Inst_q), .clk(CLK));  // open: en, clr
  Adder #(.width(20)) adder_1 (.a(NPC_q), .b(undriven), .out(adder_1_out));  // open: cin, cout
  Instruction_Decoder instruction_decoder_1 (
    .in_1(Inst_q), .OP_code(OP), .a3(instruction_decoder_1_a3), .b3(instruction_decoder_1_b3), .imm(Imm5),
    .f(Fn), .d3(instruction_decoder_1_d3), .out_8(Imm11));
  Multiplexer #(.width(32), .enable("false")) multiplexer_3 (
    .in0(ALU_Result), .in1(PC_2), .out(multiplexer_3_out), .sel(PC_Or_Result));
  Multiplexer #(.width(32), .enable("false")) multiplexer_4 (
    .in0(multiplexer_3_out), .in1(Memory_Out), .out(multiplexer_4_out), .sel(WB_Data));
  Multiplexer #(.width(3), .enable("false")) multiplexer_5 (
    .in0(instruction_decoder_1_b3), .in1(3'b111), .out(multiplexer_5_out), .sel(Rb_Or_R7));
  Multiplexer #(.width(3), .enable("false")) multiplexer_6 (
    .in0(multiplexer_5_out), .in1(instruction_decoder_1_d3), .out(multiplexer_6_out), .sel(RegDst));
  Register_File register_file_1 (
    .Ra(instruction_decoder_1_a3), .Rw(Rd4), .RegWrite(RegWrite), .BusA(register_file_1_busa),
    .BusB(register_file_1_busb), .in_6(Data), .Clock(CLK), .Rb(multiplexer_5_out));
  Register #(.width(3)) Rd2 (.D(multiplexer_6_out), .Q(Rd2_q), .clk(CLK));  // open: en, clr
  Register #(.width(20)) BTA (.D(adder_1_out), .clk(CLK));  // open: en, Q, clr
  Register #(.width(32)) A (.D(register_file_1_busa), .Q(Bus_A), .clk(CLK));  // open: en, clr
  Register #(.width(32)) B (.D(register_file_1_busb), .Q(Bus_B), .clk(CLK));  // open: en, clr
  Multiplexer #(.width(32), .enable("false")) multiplexer_7 (
    .in0(Bus_B), .in1(ExtImm5), .out(multiplexer_7_out), .sel(ALU_Src));
  ALU_Control alu_control_1 (.ALU_Op(alu_control_1_alu_op), .Op_Code(OP), .Func_Code(Fn));
  ALU alu_1 (.in_1(Bus_A), .in_3(multiplexer_7_out), .out_4(alu_1_out_4), .ALU_OP(alu_control_1_alu_op));
  Register #(.width(3)) Rd3 (.D(Rd2_q), .Q(Rd3_q), .clk(CLK));  // open: en, clr
  Register #(.width(32)) R (.D(alu_1_out_4), .Q(ALU_Result), .clk(CLK));  // open: en, clr
  Register #(.width(32)) D (.D(Bus_B), .Q(D_q), .clk(CLK));  // open: en, clr
  Data_Memory data_memory_1 (
    .in_1(ALU_Result[19:0]), .in_4(D_q), .out_6(Memory_Out), .in_2(MEM_SW), .in_5(CLK), .in_3(MEM_LD));
  Multiplexer #(.width(32), .enable("false")) multiplexer_8 (
    .in0(ALU_Result), .in1(Memory_Out), .out(multiplexer_8_out), .sel(WB_Data));
  Register #(.width(3)) u_Rd4 (.D(Rd3_q), .Q(Rd4), .clk(CLK));  // open: en, clr
  Register #(.width(32)) u_Data (.D(multiplexer_8_out), .Q(Data), .clk(CLK));  // open: en, clr

  // Other names for the same wires on the sheet: LSB_20_ALU_Result[19:0] = ALU_Result[19:0]

  // Notes on the sheet:
  //   contents of rom_1 (hex, n*v repeats v):
  //   4028 404a 8143 4121 e7fe 94c a860 8882 d880 a881
  //   Imm16 & Ext
endmodule
